# Fritzing sketch rangkaian terbaru (saved by Fritzing 0.9.3b)

parts:
  M1 = BTS7960
  M2 = BTS7960
  J1 = XL4015 DC-DC CC CV module (blue)
  J2 = XL4015 DC-DC CC CV module (blue)
  U1 = ESP32-38PinWide [part_number=ESP32-38PinWide]
  DFRobot_DFPlayer_Mini1 = DFRobot DFPlayer Mini [part_number=DFR0299]
  BAT1 = 12 battery [package=battery]
  LED2 = smd LED [color="Infrared (940nm)" package="0805 [SMD]"]
  M3 = DC Motor
  M4 = DC Motor
  C1 = Tantalum Capacitor [capacitance=1μF package="100 mil [THT, tantalum]"]
  C2 = Electrolytic Capacitor [capacitance=1µF package="100 mil [THT, electrolytic]"]
  C3 = Electrolytic Capacitor [capacitance=1µF package="100 mil [THT, electrolytic]"]
  Q1 = LTR-301 [package=ltr-301]
  LED3 = smd LED [color="Infrared (940nm)" package="0805 [SMD]"]
  LED4 = smd LED [color="Infrared (940nm)" package="0805 [SMD]"]
  LED5 = smd LED [color="Infrared (940nm)" package="0805 [SMD]"]
  LED6 = smd LED [color="Infrared (940nm)" package="0805 [SMD]"]
  LED7 = smd LED [color="Infrared (940nm)" package="0805 [SMD]"]
  LED8 = smd LED [color="Infrared (940nm)" package="0805 [SMD]"]
  Q2 = LTR-301 [package=ltr-301]
  Q3 = LTR-301 [package=ltr-301]
  Q4 = LTR-301 [package=ltr-301]
  Q5 = LTR-301 [package=ltr-301]
  Q6 = LTR-301 [package=ltr-301]
  Q7 = LTR-301 [package=ltr-301]
  R1 = Resistor [tolerance=±5% resistance=220 package=THT]
  R2 = Resistor [tolerance=±5% resistance=220 package=THT]
  R3 = Resistor [tolerance=±5% resistance=220 package=THT]
  R4 = Resistor [tolerance=±5% resistance=220 package=THT]
  R5 = Resistor [tolerance=±5% resistance=220 package=THT]
  R6 = Resistor [tolerance=±5% resistance=220 package=THT]
  R7 = Resistor [tolerance=±5% resistance=220 package=THT]
  R8 = Resistor [tolerance=±5% resistance=220 package=THT]
  R9 = Resistor [tolerance=±5% resistance=220 package=THT]
  R10 = Resistor [tolerance=±5% resistance=220 package=THT]
  R11 = Resistor [tolerance=±5% resistance=220 package=THT]
  R12 = Resistor [tolerance=±5% resistance=220 package=THT]
  R13 = Resistor [tolerance=±5% resistance=220 package=THT]
  R14 = Resistor [tolerance=±5% resistance=220 package=THT]
  F1 = Fan - Ventilador [package=THT]
  SPKR1 = Loudspeaker  # not connected
  S4 = Round Pushbutton
  C4 = Electrolytic Capacitor [capacitance=1µF package="100 mil [THT, electrolytic]"]
  C5 = Electrolytic Capacitor [capacitance=1µF package="100 mil [THT, electrolytic]"]
  S8 = SWITCH-DPDT [package=os]
  C6 = Electrolytic Capacitor [capacitance=1µF package="100 mil [THT, electrolytic]"]
  C7 = Electrolytic Capacitor [capacitance=1µF package="100 mil [THT, electrolytic]"]
  C8 = Tantalum Capacitor [capacitance=1μF package="100 mil [THT, tantalum]"]
  C9 = Tantalum Capacitor [capacitance=1μF package="100 mil [THT, tantalum]"]
  C10 = Electrolytic Capacitor [capacitance=1µF package="100 mil [THT, electrolytic]"]
  R17 = Resistor [tolerance=±5% resistance=220 package=THT]
  GM1 = GM67 Barcode Reader
  C11 = Tantalum Capacitor [capacitance=1μF package="100 mil [THT, tantalum]"]

nets:
  N1: M1.pin1, U1.GPIO25
  N2: M1.pin2, U1.GPIO26
  N3: M1.pin3, M1.pin4, M1.pin7, M2.pin5, M2.pin6, M2.pin7, DFRobot_DFPlayer_Mini1.VCC, Q1.C, Q2.C, Q3.C, Q4.C, Q5.C, Q6.C, Q7.C, R1.Pin_0, R2.Pin_0, R3.Pin_0, R4.Pin_0, R5.Pin_0, R6.Pin_0, R7.Pin_0, S8.4, C8.+, C9.+
  N4: M1.pin8, M2.pin8, DFRobot_DFPlayer_Mini1.GND-1, DFRobot_DFPlayer_Mini1.GND-2, C8.-
  N5: M1.pin9, M4.pin_2
  N6: M1.pin10, M4.pin_1
  N7: M1.pin11, M2.pin11, J1.pin_1, J2.pin_1, C2.+, C3.+, F1.5V, S4.leg1, C6.+, C7.+
  N8: M1.pin12, M2.pin12, J1.pin_2, J2.pin_2, BAT1.-, C3.-, F1.GND, C6.-, C7.-
  N9: M2.pin1, U1.GPIO27
  N10: M2.pin2, U1.GPIO14
  N11: M2.pin9, M3.pin_2
  N12: M2.pin10, M3.pin_1
  N13: J1.pin_3, C5.+, S8.2
  N14: J1.pin_4, U1.GPIO11, C1.-, C5.-
  N15: J2.pin_3, C4.+, S8.5, GM1.5V, C11.+
  N16: J2.pin_4, LED2.cathode, LED3.cathode, LED4.cathode, LED5.cathode, LED6.cathode, LED7.cathode, LED8.cathode, R12.Pin_0, C4.-, C9.-, GM1.GND, C11.-
  N17: U1.GPIO36, Q7.E, R14.Pin_1
  N18: U1.GPIO39, Q6.E, R13.Pin_1
  N19: U1.GPIO34, Q5.E, R12.Pin_1
  N20: U1.GPIO35, Q4.E, R11.Pin_1
  N21: U1.GPIO32, Q3.E, R10.Pin_1
  N22: U1.GPIO33, Q2.E, R9.Pin_1
  N23: U1.GPIO13, Q1.E, R8.Pin_1
  N24: U1.VIN, C1.+, S8.3
  N25: U1.GPIO4, DFRobot_DFPlayer_Mini1.TX
  N26: U1.GPIO16, GM1.TX
  N27: U1.GPIO17, GM1.RX
  N28: U1.GPIO5, R17.Pin_0
  N29: DFRobot_DFPlayer_Mini1.RX, R17.Pin_1
  N30: DFRobot_DFPlayer_Mini1.SPK_1, C10.+
  N31: DFRobot_DFPlayer_Mini1.SPK_2, C10.-
  N32: BAT1.+, S4.leg0
  N33: LED2.anode, R2.Pin_1
  N34: LED3.anode, R3.Pin_1
  N35: LED4.anode, R5.Pin_1
  N36: LED5.anode, R1.Pin_1
  N37: LED6.anode, R4.Pin_1
  N38: LED8.anode, R7.Pin_1

notes:
  FANDC
  ESP32
  XL4015
  BTS7960
  AKI12V
  DFDPLAYER
  SOUND
  PHOTOTRANSISTOR
  INFRARED
  MOTOR
  GM67

custom parts:
  BTS7960: BTS7960 43A Peak Power H-Bridge PWM Motor Driver
  XL4015 DC-DC CC CV module (blue): XL4015 DC-DC CC/CV module blue
  ESP32-38PinWide: Generic 38-Pin ESP32 with wide format (only access to one side of pins on a breadboard) based on Stephen Lilley's HiLetgo ESP-WROOM-32 ESP32 ESP-32S Development Board.
  12 battery: 12V lead acid type battery, like the Husqvarna YTH2448 12V 35AH battery. This is the mini version 1/4 the size of the actual battery to be closer to typical breadboard parts (around 2in wide rathher than 7in). The pads in pcb are sized to accomidate up to 14ga wire (as these batterys will deliver high currents.)
  Fan - Ventilador: Ventilador de 2 pines, se encuentra comunmente en computadoras de escritorio
  GM67 Barcode Reader: Header 8 GM67 Barcode Reader V1.0. Please ignore the PCB view of this circuit it does not matter. Please feel free to make this better
